# Fritzing sketch monitor (saved by Fritzing 0.9.2b)

parts:
  Componente1 = Arduino Pro Mini v13
  Componente2 = Adafruit BME280
  Componente3 = NRF24L01

nets:
  N1: Componente1.A4, Componente2.SDI/SDA
  N2: Componente1.A5, Componente2.SCK/SCL
  GND: Componente1.GND, Componente2.GND, Componente3.GND
  VCC: Componente1.VCC, Componente2.VIN, Componente3.VCC
  N3: Componente1.D13/SCK, Componente3.SCK
  N4: Componente1.D12/MISO, Componente3.MISO
  N5: Componente1.D11_PWM/MOSI, Componente3.MOSI
  N6: Componente1.D9_PWM, Componente3.CE
  N7: Componente1.D8, Componente3.CSN

custom parts:
  Adafruit BME280: Bosch has stepped up their game with their new BME280 sensor, an environmental sensor with temperature, barometric pressure and humidity! This sensor is great for all sorts of weather/environmental sensing and can even be used in both I2C and SPI! This precision sensor from Bosch is the best low-cost sensing solution for measuring humidity with ±3% accuracy, barometric pressure with ±1 hPa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
